// Digital circuit cpu.dig as structural Verilog
module cpu (
  input  clk,
  output [31:0] ReadData1,
  output [31:0] ReadData2
);

  wire control_unit_1_alusrc, control_unit_1_regwrite, multiplexer_1_out;
  wire [2:0] funct3;
  wire [3:0] control_unit_1_aluop;
  wire [4:0] rd, rs1, rs2;
  wire [6:0] funct7, opcode;
  wire [15:0] immediate;
  wire [31:0] add_1_s, alu_1_p4, PC_q;

  register_file register_file_1 (
    .ReadReg1(rs1), .ReadReg2(rs2), .WriteReg(rd), .WriteData(alu_1_p4), .RegWrite(control_unit_1_regwrite),
    .Clock(clk), .ReadData1(ReadData1), .ReadData2(ReadData2));
  control_unit control_unit_1 (
    .opcode(opcode), .funct3(funct3), .funct7(funct7), .ALUOp(control_unit_1_aluop),
    .ALUSrc(control_unit_1_alusrc), .RegWrite(control_unit_1_regwrite));  // open: ImmSrc
  Multiplexer multiplexer_1 (
    .sel(control_unit_1_alusrc), .in_0(ReadData2[0]), .in_1(immediate[0]), .out(multiplexer_1_out));
  // alu alu_1: pin names not known; wires that end beside it: ReadData1, multiplexer_1_out, control_unit_1_aluop, alu_1_p4
  Register #(.Bits(32), .isProgramCounter("true")) PC (.D(add_1_s), .C(clk), .en(1'b1), .Q(PC_q));
  Add #(.Bits(32)) add_1 (.a(32'h4), .b(PC_q), .c_i(1'b0), .s(add_1_s));  // open: c_o
  ROM #(.AddrBits(10), .isProgramMemory("true"), .Bits(32)) Instruction_Memory (
    .A(PC_q[11:2]), .sel(1'b1), .D({funct7, rs2, rs1, funct3, rd, opcode}));
  BitExtender bitextender_1 (.in({funct7[2:0], rs2}), .out(immediate));
  // Pins of 1 and 32 bits meet at ReadData2
  // Pins of 8 and 12 bits meet at {funct7, rs2}
  // Pins of 1 and 16 bits meet at immediate

  // Other names for the same wires on the sheet: clock = clk

  // Notes on the sheet:
  //   Instruction_Memory loads imem.mem
endmodule

/* Test case cpu:
clk ReadData1 ReadData2
*/
